// Logisim project scrittaScorrevole.circ as structural Verilog: 4 circuits, main circuit struttura
// Struttura
module struttura (
  input  Contain,
  input  [6:0] ascii,
  input  RESET_TOTALE,
  input  store,
  input  scorri,
  output clock_register,
  output [9:0] LED_SPIA,
  output Clock_kye,
  output [9:0] DATI
);

  wire and_1_out, and_2_out, and_3_out, d_ff_1_q, not_1_out, or_1_out;
  wire [9:0] bit_extender_1_out, counter_1_q, multiplier_1_out, rom_1_data;

  and and_1 (and_1_out, store, Contain);
  assign bit_extender_1_out = {{3{1'b0}}, ascii};  // Bit_Extender bit_extender_1
  Clock clock_1 (.out(clock_register));
  D_Flip_Flop d_ff_1 (.clk(not_1_out), .D(and_1_out), .Q(d_ff_1_q));  // open: Qn, preset, en, reset
  not not_1 (not_1_out, clock_register);
  and and_2 (and_2_out, Contain, clock_register, d_ff_1_q);
  and and_3 (and_3_out, clock_register, scorri);
  Multiplier #(.width(10)) multiplier_1 (.a(bit_extender_1_out), .b(10'h6), .out(multiplier_1_out));  // open: cin, cout
  or or_1 (or_1_out, and_2_out, and_3_out);
  Counter #(.width(10), .max('h5)) counter_1 (
    .Q(counter_1_q), .carry(Clock_kye), .clk(and_2_out), .clr(RESET_TOTALE));  // open: load, D, count
  Adder #(.width(10)) adder_1 (.a(multiplier_1_out), .b(counter_1_q), .out(LED_SPIA));  // open: cin, cout
  ROM #(.addrWidth(10), .dataWidth(10)) rom_1 (.addr(LED_SPIA), .data(rom_1_data));  // open: sel
  ram_e_altro RAM_e_ALTRO (
    .in_1(rom_1_data), .clock(or_1_out), .read_write(d_ff_1_q), .reset(RESET_TOTALE), .out_5(DATI));

  // Notes on the sheet:
  //   contents of rom_1 (hex, n*v repeats v):
  //   1 2 3 4 5 6 20 21 22 23 24 25 30 31 32 33 34 35 40 41 42 43 44 45 7f 3f 3f 3f 3c 170*0 180 3e8 180 0
  //   0 0 300 0 300 0 0 120 3f0 120 3f0 120 21*0 300 40*0 18 18 9*0 1f0 208 208 208 1f0 0 0 108 3f8 8 0 0
  //   108 218 228 248 188 0 110 208 248 248 1b0 0 60 a0 120 3f8 20 0 3d0 248 248 248 30 0 1f0 248 248 248
  //   30 0 200 200 278 280 300 0 1b0 248 248 248 1b0 0 188 248 248 248 1f0 43*0 1f8 220 220 220 1f8 0 3f8
  //   248 248 248 1b0 0 1f0 208 208 208 110 0 3f8 208 208 208 1f0 0 3f8 248 248 248 208 0 3f8 240 240 240
  //   200 0 1f0 208 208 228 130 0 3f8 40 40 40 3f8 0 0 208 3f8 208 0 0 10 8 8 8 3f0 0 3f8 40 a0 110 208 0
  //   3f8 4*8 0 3f8 100 80 100 3f8 0 3f8 180 40 30 3f8 0 1f0 208 208 208 1f0 0 3f8 240 240 240 180 0 1f0
  //   208 228 218 1f8 0 3f8 240 260 250 188 0 190 248 248 248 130 0 200 200 3f8 200 200 0 3f0 8 8 8 3f0 0
  //   3e0 10 8 10 3e0 0 3f0 8 70 8 3f0 0 208 1b0 40 1b0 208 0 200 100 f8 100 200 0 218 228 248 288 308
  //   37*0 70 88 88 f0 8 0 3f8 88 88 88 70 0 70 4*88 0 70 88 88 88 3f8 0 70 a8 a8 a8 48 0 0 88 1f8 288 0 0
  //   72 89 89 89 fe 0 3f8 80 80 80 78 0 0 88 2f8 8 0 0 0 2 81 2fe 0 0 3f8 20 50 88 0 0 0 208 3f8 8 0 0 f8
  //   80 78 80 78 0 f8 40 80 80 78 0 70 88 88 88 70 0 ff 88 88 88 70 0 70 88 88 88 ff 0 f8 40 80 80 40 0
  //   48 a8 a8 a8 90 0 0 80 3f0 88 0 0 f0 8 8 10 f8 0 e0 10 8 10 e0 0 f0 8 30 8 f0 0 88 50 20 50 88 0 f2 9
  //   9 9 fe 0 88 98 a8 c8 88
endmodule

module ram_e_altro (
  input  [9:0] in_1,
  input  clock,
  input  read_write,
  input  reset,
  output [9:0] out_5
);

  wire and_1_out, and_2_out, and_3_out, and_4_out, and_5_out, counter_2_carry, not_1_out, not_2_out, or_1_out;
  wire [9:0] counter_1_q, counter_3_q;

  and and_1 (and_1_out, read_write, 1'b1);
  RAM #(.addrWidth(10), .dataWidth(10), .bus("separate")) ram_1 (
    .addr(counter_3_q), .din(in_1), .data(out_5), .str(and_1_out), .sel(1'b1), .clk(clock), .ld(and_2_out),
    .clr(reset));
  and and_2 (and_2_out, ~read_write, 1'b1);  // AND_Gate
  and and_3 (and_3_out, ~and_2_out, clock);  // AND_Gate
  Counter #(.width(10), .max('h3ff)) counter_1 (
    .Q(counter_1_q), .clk(and_3_out), .clr(reset));  // open: load, D, count, carry
  Counter #(.width(10), .max('h3ff), .ongoal("load")) counter_2 (
    .load(and_2_out), .D(counter_1_q), .carry(counter_2_carry), .clk(clock), .clr(reset));  // open: count, Q
  not not_1 (not_1_out, not_2_out);
  not not_2 (not_2_out, counter_2_carry);
  and and_4 (and_4_out, and_2_out, ~and_2_out);  // AND_Gate
  Counter #(.width(10), .max('h3ff)) counter_3 (
    .Q(counter_3_q), .clk(clock), .clr(or_1_out));  // open: load, D, count, carry
  and and_5 (and_5_out, not_2_out, not_1_out);
  or or_1 (or_1_out, and_5_out, and_5_out, and_4_out, reset);
endmodule

// BANCO REGISTRI
module banco_registri (
  input  reset,
  input  [9:0] IN,
  input  clock,
  output [9:0] out_4,
  output [9:0] out_5,
  output [9:0] out_6,
  output [9:0] out_7,
  output [9:0] out_8,
  output [9:0] out_9,
  output [9:0] out_10,
  output [9:0] out_11,
  output [9:0] out_12,
  output [9:0] out_13,
  output [9:0] out_14,
  output [9:0] out_15,
  output [9:0] out_16,
  output [9:0] out_17,
  output [9:0] out_18,
  output [9:0] out_19,
  output [9:0] out_20,
  output [9:0] out_21,
  output [9:0] out_22,
  output [9:0] out_23,
  output [9:0] out_24,
  output [9:0] out_25,
  output [9:0] out_26,
  output [9:0] out_27,
  output [9:0] out_28,
  output [9:0] out_29,
  output [9:0] out_30,
  output [9:0] out_31,
  output [9:0] out_32,
  output [9:0] out_33,
  output [9:0] out_34,
  output [9:0] out_35,
  output [9:0] out_36
);

  Register #(.width(10)) register_1 (.D(IN), .Q(out_4), .clk(clock), .clr(reset));  // open: en
  Register #(.width(10)) register_2 (.D(out_19), .Q(out_20), .clk(clock), .clr(reset));  // open: en
  Register #(.width(10)) register_3 (.D(out_5), .Q(out_6), .clk(clock), .clr(reset));  // open: en
  Register #(.width(10)) register_4 (.D(out_4), .Q(out_5), .clk(clock), .clr(reset));  // open: en
  Register #(.width(10)) register_5 (.D(out_20), .Q(out_21), .clk(clock), .clr(reset));  // open: en
  Register #(.width(10)) register_6 (.D(out_21), .Q(out_22), .clk(clock), .clr(reset));  // open: en
  Register #(.width(10)) register_7 (.D(out_6), .Q(out_7), .clk(clock), .clr(reset));  // open: en
  Register #(.width(10)) register_8 (.D(out_22), .Q(out_23), .clk(clock), .clr(reset));  // open: en
  Register #(.width(10)) register_9 (.D(out_7), .Q(out_8), .clk(clock), .clr(reset));  // open: en
  Register #(.width(10)) register_10 (.D(out_8), .Q(out_9), .clk(clock), .clr(reset));  // open: en
  Register #(.width(10)) register_11 (.D(out_23), .Q(out_24), .clk(clock), .clr(reset));  // open: en
  Register #(.width(10)) register_12 (.D(out_24), .Q(out_25), .clk(clock), .clr(reset));  // open: en
  Register #(.width(10)) register_13 (.D(out_9), .Q(out_10), .clk(clock), .clr(reset));  // open: en
  Register #(.width(10)) register_14 (.D(out_25), .Q(out_26), .clk(clock), .clr(reset));  // open: en
  Register #(.width(10)) register_15 (.D(out_26), .Q(out_27), .clk(clock), .clr(reset));  // open: en
  Register #(.width(10)) register_16 (.D(out_11), .Q(out_12), .clk(clock), .clr(reset));  // open: en
  Register #(.width(10)) register_17 (.D(out_10), .Q(out_11), .clk(clock), .clr(reset));  // open: en
  Register #(.width(10)) register_18 (.D(out_27), .Q(out_28), .clk(clock), .clr(reset));  // open: en
  Register #(.width(10)) register_19 (.D(out_13), .Q(out_14), .clk(clock), .clr(reset));  // open: en
  Register #(.width(10)) register_20 (.D(out_12), .Q(out_13), .clk(clock), .clr(reset));  // open: en
  Register #(.width(10)) register_21 (.D(out_28), .Q(out_29), .clk(clock), .clr(reset));  // open: en
  Register #(.width(10)) register_22 (.D(out_29), .Q(out_30), .clk(clock), .clr(reset));  // open: en
  Register #(.width(10)) register_23 (.D(out_14), .Q(out_15), .clk(clock), .clr(reset));  // open: en
  Register #(.width(10)) register_24 (.D(out_30), .Q(out_31), .clk(clock), .clr(reset));  // open: en
  Register #(.width(10)) register_25 (.D(out_16), .Q(out_17), .clk(clock), .clr(reset));  // open: en
  Register #(.width(10)) register_26 (.D(out_15), .Q(out_16), .clk(clock), .clr(reset));  // open: en
  Register #(.width(10)) register_27 (.D(out_31), .Q(out_32), .clk(clock), .clr(reset));  // open: en
  Register #(.width(10)) register_28 (.D(out_32), .Q(out_33), .clk(clock), .clr(reset));  // open: en
  Register #(.width(10)) register_29 (.D(out_17), .Q(out_18), .clk(clock), .clr(reset));  // open: en
  Register #(.width(10)) register_30 (.D(out_34), .Q(out_35), .clk(clock), .clr(reset));  // open: en
  Register #(.width(10)) register_31 (.D(out_33), .Q(out_34), .clk(clock), .clr(reset));  // open: en
  Register #(.width(10)) register_32 (.D(out_18), .Q(out_19), .clk(clock), .clr(reset));  // open: en

  assign out_36 = out_35;
endmodule

module main1 (
  input  STORE,
  input  SCORRI
);

  wire keyboard_1_avail, RESET_out, struttura_1_clock_kye, struttura_1_clock_register;
  wire [6:0] keyboard_1_data;
  wire [9:0] banco_registri_1_out_4, banco_registri_1_out_5, banco_registri_1_out_6, banco_registri_1_out_7,
       banco_registri_1_out_8, banco_registri_1_out_9, banco_registri_1_out_10, banco_registri_1_out_11,
       banco_registri_1_out_12, banco_registri_1_out_13, banco_registri_1_out_14, banco_registri_1_out_15,
       banco_registri_1_out_16, banco_registri_1_out_17, banco_registri_1_out_18, banco_registri_1_out_19,
       banco_registri_1_out_20, banco_registri_1_out_21, banco_registri_1_out_22, banco_registri_1_out_23,
       banco_registri_1_out_24, banco_registri_1_out_25, banco_registri_1_out_26, banco_registri_1_out_27,
       banco_registri_1_out_28, banco_registri_1_out_29, banco_registri_1_out_30, banco_registri_1_out_31,
       banco_registri_1_out_32, banco_registri_1_out_33, banco_registri_1_out_34, banco_registri_1_out_35,
       banco_registri_2_out_4, banco_registri_2_out_5, banco_registri_2_out_6, banco_registri_2_out_7,
       banco_registri_2_out_8, banco_registri_2_out_9, banco_registri_2_out_10, banco_registri_2_out_11,
       banco_registri_2_out_12, banco_registri_2_out_13, banco_registri_2_out_14, banco_registri_2_out_15,
       banco_registri_2_out_16, banco_registri_2_out_17, banco_registri_2_out_18, banco_registri_2_out_19,
       banco_registri_2_out_20, banco_registri_2_out_21, banco_registri_2_out_22, banco_registri_2_out_23,
       banco_registri_2_out_24, banco_registri_2_out_25, banco_registri_2_out_26, banco_registri_2_out_27,
       banco_registri_2_out_28, banco_registri_2_out_29, banco_registri_2_out_30, banco_registri_2_out_31,
       banco_registri_2_out_32, banco_registri_2_out_33, banco_registri_2_out_34, banco_registri_2_out_35,
       banco_registri_2_out_36, banco_registri_3_out_4, banco_registri_3_out_5, banco_registri_3_out_6,
       banco_registri_3_out_7, banco_registri_3_out_8, banco_registri_3_out_9, banco_registri_3_out_10,
       banco_registri_3_out_11, banco_registri_3_out_12, banco_registri_3_out_13, banco_registri_3_out_14,
       banco_registri_3_out_15, banco_registri_3_out_16, banco_registri_3_out_17, banco_registri_3_out_18,
       banco_registri_3_out_19, banco_registri_3_out_20, banco_registri_3_out_21, banco_registri_3_out_22,
       banco_registri_3_out_23, banco_registri_3_out_24, banco_registri_3_out_25, banco_registri_3_out_26,
       banco_registri_3_out_27, banco_registri_3_out_28, banco_registri_3_out_29, banco_registri_3_out_30,
       banco_registri_3_out_31, banco_registri_3_out_32, banco_registri_3_out_33, banco_registri_3_out_34,
       banco_registri_3_out_35, banco_registri_3_out_36, struttura_1_dati, struttura_1_led_spia;

  DotMatrix #(.matrixcols(32), .matrixrows(10)) dotmatrix_1 (
    .col0(banco_registri_1_out_35), .col1(banco_registri_1_out_34), .col2(banco_registri_1_out_33),
    .col3(banco_registri_1_out_32), .col4(banco_registri_1_out_31), .col5(banco_registri_1_out_30),
    .col6(banco_registri_1_out_29), .col7(banco_registri_1_out_28), .col8(banco_registri_1_out_27),
    .col9(banco_registri_1_out_26), .col10(banco_registri_1_out_25), .col11(banco_registri_1_out_24),
    .col12(banco_registri_1_out_23), .col13(banco_registri_1_out_22), .col14(banco_registri_1_out_21),
    .col15(banco_registri_1_out_20), .col16(banco_registri_1_out_19), .col17(banco_registri_1_out_18),
    .col18(banco_registri_1_out_17), .col19(banco_registri_1_out_16), .col20(banco_registri_1_out_15),
    .col21(banco_registri_1_out_14), .col22(banco_registri_1_out_13), .col23(banco_registri_1_out_12),
    .col24(banco_registri_1_out_11), .col25(banco_registri_1_out_10), .col26(banco_registri_1_out_9),
    .col27(banco_registri_1_out_8), .col28(banco_registri_1_out_7), .col29(banco_registri_1_out_6),
    .col30(banco_registri_1_out_5), .col31(banco_registri_1_out_4));
  Keyboard #(.buflen(128), .trigger("falling")) keyboard_1 (
    .clk(struttura_1_clock_kye), .clr(RESET_out), .avail(keyboard_1_avail), .data(keyboard_1_data));  // open: re
  banco_registri banco_registri_1 (
    .out_4(banco_registri_1_out_4), .out_5(banco_registri_1_out_5), .out_6(banco_registri_1_out_6),
    .out_7(banco_registri_1_out_7), .out_8(banco_registri_1_out_8), .out_9(banco_registri_1_out_9),
    .out_10(banco_registri_1_out_10), .out_11(banco_registri_1_out_11), .out_12(banco_registri_1_out_12),
    .out_13(banco_registri_1_out_13), .out_14(banco_registri_1_out_14), .out_15(banco_registri_1_out_15),
    .out_16(banco_registri_1_out_16), .out_17(banco_registri_1_out_17), .out_18(banco_registri_1_out_18),
    .out_19(banco_registri_1_out_19), .out_20(banco_registri_1_out_20), .out_21(banco_registri_1_out_21),
    .out_22(banco_registri_1_out_22), .out_23(banco_registri_1_out_23), .out_24(banco_registri_1_out_24),
    .out_25(banco_registri_1_out_25), .out_26(banco_registri_1_out_26), .out_27(banco_registri_1_out_27),
    .out_28(banco_registri_1_out_28), .out_29(banco_registri_1_out_29), .out_30(banco_registri_1_out_30),
    .out_31(banco_registri_1_out_31), .out_32(banco_registri_1_out_32), .out_33(banco_registri_1_out_33),
    .out_34(banco_registri_1_out_34), .out_35(banco_registri_1_out_35), .IN(banco_registri_2_out_36),
    .reset(RESET_out), .clock(struttura_1_clock_register));  // open: out_36
  DotMatrix #(.matrixcols(1), .matrixrows(10)) dotmatrix_2 (.col0(struttura_1_led_spia));
  struttura struttura_1 (
    .Clock_kye(struttura_1_clock_kye), .ascii(keyboard_1_data), .RESET_TOTALE(RESET_out), .store(STORE),
    .scorri(SCORRI), .Contain(keyboard_1_avail), .clock_register(struttura_1_clock_register),
    .LED_SPIA(struttura_1_led_spia), .DATI(struttura_1_dati));
  Button RESET (.out(RESET_out));
  DotMatrix #(.matrixcols(32), .matrixrows(10)) dotmatrix_3 (
    .col0(banco_registri_2_out_35), .col1(banco_registri_2_out_34), .col2(banco_registri_2_out_33),
    .col3(banco_registri_2_out_32), .col4(banco_registri_2_out_31), .col5(banco_registri_2_out_30),
    .col6(banco_registri_2_out_29), .col7(banco_registri_2_out_28), .col8(banco_registri_2_out_27),
    .col9(banco_registri_2_out_26), .col10(banco_registri_2_out_25), .col11(banco_registri_2_out_24),
    .col12(banco_registri_2_out_23), .col13(banco_registri_2_out_22), .col14(banco_registri_2_out_21),
    .col15(banco_registri_2_out_20), .col16(banco_registri_2_out_19), .col17(banco_registri_2_out_18),
    .col18(banco_registri_2_out_17), .col19(banco_registri_2_out_16), .col20(banco_registri_2_out_15),
    .col21(banco_registri_2_out_14), .col22(banco_registri_2_out_13), .col23(banco_registri_2_out_12),
    .col24(banco_registri_2_out_11), .col25(banco_registri_2_out_10), .col26(banco_registri_2_out_9),
    .col27(banco_registri_2_out_8), .col28(banco_registri_2_out_7), .col29(banco_registri_2_out_6),
    .col30(banco_registri_2_out_5), .col31(banco_registri_2_out_4));
  banco_registri banco_registri_2 (
    .out_4(banco_registri_2_out_4), .out_5(banco_registri_2_out_5), .out_6(banco_registri_2_out_6),
    .out_7(banco_registri_2_out_7), .out_8(banco_registri_2_out_8), .out_9(banco_registri_2_out_9),
    .out_10(banco_registri_2_out_10), .out_11(banco_registri_2_out_11), .out_12(banco_registri_2_out_12),
    .out_13(banco_registri_2_out_13), .out_14(banco_registri_2_out_14), .out_15(banco_registri_2_out_15),
    .out_16(banco_registri_2_out_16), .out_17(banco_registri_2_out_17), .out_18(banco_registri_2_out_18),
    .out_19(banco_registri_2_out_19), .out_20(banco_registri_2_out_20), .out_21(banco_registri_2_out_21),
    .out_22(banco_registri_2_out_22), .out_23(banco_registri_2_out_23), .out_24(banco_registri_2_out_24),
    .out_25(banco_registri_2_out_25), .out_26(banco_registri_2_out_26), .out_27(banco_registri_2_out_27),
    .out_28(banco_registri_2_out_28), .out_29(banco_registri_2_out_29), .out_30(banco_registri_2_out_30),
    .out_31(banco_registri_2_out_31), .out_32(banco_registri_2_out_32), .out_33(banco_registri_2_out_33),
    .out_34(banco_registri_2_out_34), .out_35(banco_registri_2_out_35), .out_36(banco_registri_2_out_36),
    .IN(banco_registri_3_out_36), .reset(RESET_out), .clock(struttura_1_clock_register));
  DotMatrix #(.matrixcols(32), .matrixrows(10)) dotmatrix_4 (
    .col0(banco_registri_3_out_35), .col1(banco_registri_3_out_34), .col2(banco_registri_3_out_33),
    .col3(banco_registri_3_out_32), .col4(banco_registri_3_out_31), .col5(banco_registri_3_out_30),
    .col6(banco_registri_3_out_29), .col7(banco_registri_3_out_28), .col8(banco_registri_3_out_27),
    .col9(banco_registri_3_out_26), .col10(banco_registri_3_out_25), .col11(banco_registri_3_out_24),
    .col12(banco_registri_3_out_23), .col13(banco_registri_3_out_22), .col14(banco_registri_3_out_21),
    .col15(banco_registri_3_out_20), .col16(banco_registri_3_out_19), .col17(banco_registri_3_out_18),
    .col18(banco_registri_3_out_17), .col19(banco_registri_3_out_16), .col20(banco_registri_3_out_15),
    .col21(banco_registri_3_out_14), .col22(banco_registri_3_out_13), .col23(banco_registri_3_out_12),
    .col24(banco_registri_3_out_11), .col25(banco_registri_3_out_10), .col26(banco_registri_3_out_9),
    .col27(banco_registri_3_out_8), .col28(banco_registri_3_out_7), .col29(banco_registri_3_out_6),
    .col30(banco_registri_3_out_5), .col31(banco_registri_3_out_4));
  banco_registri banco_registri_3 (
    .out_4(banco_registri_3_out_4), .out_5(banco_registri_3_out_5), .out_6(banco_registri_3_out_6),
    .out_7(banco_registri_3_out_7), .out_8(banco_registri_3_out_8), .out_9(banco_registri_3_out_9),
    .out_10(banco_registri_3_out_10), .out_11(banco_registri_3_out_11), .out_12(banco_registri_3_out_12),
    .out_13(banco_registri_3_out_13), .out_14(banco_registri_3_out_14), .out_15(banco_registri_3_out_15),
    .out_16(banco_registri_3_out_16), .out_17(banco_registri_3_out_17), .out_18(banco_registri_3_out_18),
    .out_19(banco_registri_3_out_19), .out_20(banco_registri_3_out_20), .out_21(banco_registri_3_out_21),
    .out_22(banco_registri_3_out_22), .out_23(banco_registri_3_out_23), .out_24(banco_registri_3_out_24),
    .out_25(banco_registri_3_out_25), .out_26(banco_registri_3_out_26), .out_27(banco_registri_3_out_27),
    .out_28(banco_registri_3_out_28), .out_29(banco_registri_3_out_29), .out_30(banco_registri_3_out_30),
    .out_31(banco_registri_3_out_31), .out_32(banco_registri_3_out_32), .out_33(banco_registri_3_out_33),
    .out_34(banco_registri_3_out_34), .out_35(banco_registri_3_out_35), .out_36(banco_registri_3_out_36),
    .IN(struttura_1_dati), .reset(RESET_out), .clock(struttura_1_clock_register));

  // Notes on the sheet:
  //   MATRICI LED
  //   DATI
endmodule
